# Fritzing sketch breadboard (saved by Fritzing 0.9.3b)
breadboards: 1

parts:
  BeagleBone1 = BeagleBone Black
  R1 = Resistor [tolerance=±5% resistance=1k package=THT]
  LED1 = LED - 5mm [color="Red (633nm)" package="5 mm [THT]"]
  S1 = Toggle Switch [package=THT]

nets:
  N1: BeagleBone1.no_name_yet#2, R1.Pin_0
  N2: BeagleBone1.no_name_yet#4, S1.L2
  N3: BeagleBone1.no_name_yet#112, LED1.anode
  N4: BeagleBone1.no_name_yet#114, S1.COM
  N5: R1.Pin_1, LED1.cathode

custom parts:
  BeagleBone Black: BeagleBone Black rev. A5B
